# Fritzing sketch MicroPython_Jupyter (saved by Fritzing 0.9.3b)
breadboards: 1

parts:
  U1 = NodeMCU V1.0
  R1 = Resistor [tolerance=±5% resistance=220 package=THT]
  S2 = Pushbutton [package="[THT]"]
  J1 = Basic Servo
  R2 = Photocell (LDR) [package=THT]
  R3 = Resistor [tolerance=±5% resistance=10k package=THT]
  LED2 = LED - 5mm [color="Red (633nm)" package="5 mm [THT]"]
  Ext_Temperature_Sensor1 = DS18B20 1-Wire Temperature Sensor [part_number=DS18B20]
  R5 = Resistor [tolerance=±5% resistance=4.7k package=THT]
  R4 = Resistor [tolerance=±5% resistance=4.7k package=THT]
  DHT22 = Humidity and Temperature Sensor RHT03 [part_number="TEMP/HUM SENSOR"]
  OLED_I2C2 = OLED 128x64 I2C Monochrome Display  # not connected

nets:
  N1: U1.D3, LED2.anode
  N2: U1.D4, Ext_Temperature_Sensor1.DQ, R5.Pin_1
  VCC: U1.3V3, J1.vcc, R2.pin_0, R4.Pin_1, DHT22.Vcc
  GND: U1.GND, R1.Pin_0, S2.Pin_3, S2.Pin_4, J1.gnd, R3.Pin_1, Ext_Temperature_Sensor1.GND, DHT22.GND_2
  N3: U1.D5, J1.pulse
  N4: U1.D6, R4.Pin_0, DHT22.Data-signal
  N5: U1.D7, S2.Pin_1, S2.Pin_2
  N6: U1.A0, R2.pin_1, R3.Pin_0
  N7: R1.Pin_1, LED2.cathode
  N8: Ext_Temperature_Sensor1.VDD, R5.Pin_0

notes:
  D3 (pin 0)
  D7 (pin 13)
  D5 (pin 14)
  A0
  D4 (pin 2)
  D1(pin 5)
  D2(pin 4)

custom parts:
  NodeMCU V1.0: ESP8266 based NodeMCU
