# Fritzing sketch Jupyter-RPi-Sensors-GPIO (saved by Fritzing 0.9.3b)
breadboards: 1

parts:
  R1 = Resistor [tolerance=±5% resistance=330 package=THT]
  LED1 = LED - 5mm [color="Red (633nm)" package="5 mm [THT]"]
  Raspberry_Pi_1 = Raspberry Pi 3 [part_number=RPI-3-V1.2]
  LED2 = LED - 5mm [color="Yellow (595nm)" package="5 mm [THT]"]
  R2 = Resistor [tolerance=±5% resistance=330 package=THT]
  LED3 = LED - 5mm [color="Green (560nm)" package="5 mm [THT]"]
  R3 = Resistor [tolerance=±5% resistance=330 package=THT]
  S1 = Pushbutton [package="[THT]"]
  R4 = Resistor [tolerance=±5% resistance=330 package=THT]
  DHT22 = Humidity and Temperature Sensor RHT03 [part_number="TEMP/HUM SENSOR"]
  R5 = Resistor [tolerance=±5% resistance=4.7k package=THT]
  Ext_Temperature_Sensor = DS18B20 1-Wire Temperature Sensor [part_number=DS18B20]
  R6 = Resistor [tolerance=±5% resistance=4.7k package=THT]
  TEMP/PRESS/ALT_Sensor = Barometric Pressure Sensor - BMP180 Breakout (GY-68)

nets:
  N1: R1.Pin_0, LED1.cathode
  GND: R1.Pin_1, Raspberry_Pi_1.GND, R2.Pin_1, R3.Pin_1, R4.Pin_1, DHT22.GND_2, Ext_Temperature_Sensor.GND, TEMP/PRESS/ALT_Sensor.GND
  N2: LED1.anode, Raspberry_Pi_1.GIPO13
  VCC: Raspberry_Pi_1.3v3, S1.Pin_3, S1.Pin_4, DHT22.Vcc, R5.Pin_0, Ext_Temperature_Sensor.VDD, R6.Pin_0, TEMP/PRESS/ALT_Sensor.VCC
  N3: Raspberry_Pi_1.GPIO2, TEMP/PRESS/ALT_Sensor.SDA
  N4: Raspberry_Pi_1.GPIO3, TEMP/PRESS/ALT_Sensor.SCL
  N5: Raspberry_Pi_1.GIPO4, Ext_Temperature_Sensor.DQ, R6.Pin_1
  N6: Raspberry_Pi_1.GIPO19, LED2.anode
  N7: Raspberry_Pi_1.GIPO26, LED3.anode
  N8: Raspberry_Pi_1.GIPO20, S1.Pin_1, S1.Pin_2, R4.Pin_0
  N9: Raspberry_Pi_1.GIPO16, DHT22.Data-signal, R5.Pin_1
  N10: LED2.cathode, R2.Pin_0
  N11: LED3.cathode, R3.Pin_0

notes:
  GPIO 13
  GPIO 19
  GPIO 20
  GPIO 26
  3.3V
  GPIO 16
  GPIO 4
  GPIO 2 - SDA
  GPIO 3 - SCL
